# Fritzing sketch 벤츠_회로도 (saved by Fritzing 0.9.3b)
breadboards: 1

parts:
  LED1 = smd LED [color="Red (633nm)" package="0805 [SMD]"]
  LED2 = smd LED [color="Red (633nm)" package="0805 [SMD]"]
  LED9 = smd LED [color="Orange (605nm)" package="0805 [SMD]"]
  LED10 = smd LED [color="Orange (605nm)" package="0805 [SMD]"]
  LED11 = smd LED [color="Orange (605nm)" package="0805 [SMD]"]
  LED12 = smd LED [color="Orange (605nm)" package="0805 [SMD]"]
  LED13 = smd LED [color="White (8000K)" package="0805 [SMD]"]
  LED14 = smd LED [color="White (8000K)" package="0805 [SMD]"]
  Raspberry_Pi_1 = Raspberry Pi 3 [part_number=RPI-3-V1.2]
  L298N1 = L298N DC motor driver
  M3 = DC Motor
  VCC1 = Battery block 9V
  M5 = DC Motor
  MCP1 = MCP3208
  R1 = Resistor [tolerance=±5% resistance=220 package=THT]
  R2 = Photocell (LDR) [package=THT]
  LED15 = smd LED [color="Red (633nm)" package="0805 [SMD]"]

nets:
  GND: LED1.cathode, LED2.cathode, LED9.cathode, LED10.cathode, LED11.cathode, LED12.cathode, LED13.cathode, LED14.cathode, Raspberry_Pi_1.GND, L298N1.GND, VCC1.-, MCP1.Chan_0, MCP1.Chan_5, R1.Pin_1, LED15.cathode
  N1: LED1.anode, LED2.anode, Raspberry_Pi_1.GPIO6
  N2: LED9.anode, LED10.anode, Raspberry_Pi_1.GPIO2
  N3: LED11.anode, LED12.anode, Raspberry_Pi_1.GPIO3
  N4: LED13.anode, LED14.anode, Raspberry_Pi_1.GPIO4
  N5: Raspberry_Pi_1.GPIO17, L298N1.ENA
  N6: Raspberry_Pi_1.GPIO27, L298N1.IN1
  N7: Raspberry_Pi_1.GPIO22, L298N1.IN2
  N8: Raspberry_Pi_1.GPIO10, MCP1.Chan_4
  N9: Raspberry_Pi_1.GPIO9, MCP1.Chan_3
  N10: Raspberry_Pi_1.GPIO11, MCP1.Chan_2
  N11: Raspberry_Pi_1.GPIO13, L298N1.IN3
  N12: Raspberry_Pi_1.GPIO19, L298N1.IN4
  N13: Raspberry_Pi_1.GPIO26, L298N1.ENB
  N14: Raspberry_Pi_1.GPIO8, MCP1.Chan_1
  N15: Raspberry_Pi_1.GPIO18, LED15.anode
  N16: Raspberry_Pi_1.5V, MCP1.Chan_6, MCP1.Chan_7
  N17: L298N1.OUT1, M3.pin_2
  N18: L298N1.OUT2, M3.pin_1
  N19: L298N1.OUT3, M5.pin_2
  N20: L298N1.OUT4, M5.pin_1
  N21: L298N1.12V, VCC1.+
  N22: MCP1.CS/SHDN, R2.pin_1
  N23: R1.Pin_0, R2.pin_0

notes:
  LED GPIO:2(L 방향),3(R 방향),4(전조등),6(브레이크등)
  MOTOR GPIO:17,27,22,10,9,11
  SENSOR GPIO:18(CDS)

custom parts:
  L298N DC motor driver: 2x DC motor driver with 78M05 positive voltage regulator (7..35 V) L298N: max 46 V, 2 A Set 5 V Enable jumper to enable 5 V regultor (needed for the L298N) and +5 V output at screw terminal or supply external +5 V at screw terminal Set ENA and/or ENB to +5 V to enable motor permanently or supply ENA and/or ENB with PWM signal IN1 and IN2 set rotation directory for motor A (OUT1/OUT2) IN2 and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
